// Logisim project Control Unit.circ as structural Verilog: 1 circuit, main circuit main
module main (
  input  [2:0] Function,
  input  [3:0] OPcode
);

  wire nor_1_out, nor_2_out, not_1_out;
  wire [4:0] bit_extender_1_out, multiplexer_1_out, multiplexer_2_out;

  assign bit_extender_1_out = {{1{1'b1}}, OPcode};  // Bit_Extender bit_extender_1
  not not_1 (not_1_out, OPcode[0]);
  nor nor_1 (nor_1_out, not_1_out, OPcode[1], OPcode[2], OPcode[3]);
  nor nor_2 (nor_2_out, OPcode[0], OPcode[1], OPcode[2], OPcode[3]);
  Multiplexer #(.width(5), .enable("false")) multiplexer_1 (
    .in0(bit_extender_1_out), .in1({2'b00, Function}), .out(multiplexer_1_out), .sel(nor_2_out));
  Multiplexer #(.width(5), .enable("false")) multiplexer_2 (
    .in0(multiplexer_1_out), .in1({2'b01, Function}), .out(multiplexer_2_out), .sel(nor_1_out));
endmodule
