// Logisim project alu.circ as structural Verilog: 1 circuit, main circuit main
module main (
  input  [15:0] A,
  input  [15:0] B,
  input  [3:0] ALU_CONT,
  output [15:0] out_4
);

  wire comparator_1_eq, comparator_1_lt, comparator_2_eq, comparator_2_lt, or_2_out, or_3_out;
  wire [15:0] adder_1_out, and_2_out, and_3_out, AND_out, bit_extender_1_out, bit_extender_2_out,
       bit_extender_3_out, bit_extender_4_out, bit_extender_5_out, FIRST_HALF, not_1_out, not_2_out,
       not_3_out, OR_out, R, SECOND_HALF, SL, SR, SRA, xor_1_out, XOR_2_out;

  assign not_1_out = ~A;  // NOT_Gate not_1, 16 bits wide
  assign not_2_out = ~B;  // NOT_Gate not_2, 16 bits wide
  assign bit_extender_1_out = {{15{ALU_CONT[0]}}, ALU_CONT[0]};  // Bit_Extender bit_extender_1
  assign AND_out = A & B;  // AND_Gate AND, 16 bits wide
  assign OR_out = A | B;  // OR_Gate OR, 16 bits wide
  assign and_2_out = not_1_out & B;  // AND_Gate and_2, 16 bits wide
  assign and_3_out = not_2_out & A;  // AND_Gate and_3, 16 bits wide
  Shifter #(.width(16)) shifter_1 (.in(A), .\dist (B[3:0]), .out(SL));
  Shifter #(.width(16), .shift("lr")) shifter_2 (.in(A), .\dist (B[3:0]), .out(SR));
  Shifter #(.width(16), .shift("ar")) shifter_3 (.in(A), .\dist (B[3:0]), .out(SRA));
  Shifter #(.width(16), .shift("rl")) shifter_4 (.in(A), .\dist (B[3:0]), .out(R));
  assign xor_1_out = B ^ bit_extender_1_out;  // XOR_Gate xor_1, 16 bits wide
  Comparator #(.width(16)) comparator_1 (.a(A), .b(B), .eq(comparator_1_eq), .lt(comparator_1_lt));  // open: gt
  Comparator #(.width(16), .mode("unsigned")) comparator_2 (
    .a(A), .b(B), .eq(comparator_2_eq), .lt(comparator_2_lt));  // open: gt
  Adder #(.width(16)) adder_1 (.a(xor_1_out), .b(A), .out(adder_1_out), .cin(ALU_CONT[0]));  // open: cout
  or or_2 (or_2_out, comparator_1_eq, comparator_1_lt);
  or or_3 (or_3_out, comparator_2_eq, comparator_2_lt);
  assign XOR_2_out = and_2_out | and_3_out;  // OR_Gate XOR_2, 16 bits wide
  assign bit_extender_2_out = {{15{1'b0}}, comparator_1_lt};  // Bit_Extender bit_extender_2
  assign bit_extender_3_out = {{15{1'b0}}, or_2_out};  // Bit_Extender bit_extender_3
  assign bit_extender_4_out = {{15{1'b0}}, comparator_2_lt};  // Bit_Extender bit_extender_4
  assign not_3_out = ~OR_out;  // NOT_Gate not_3, 16 bits wide
  assign bit_extender_5_out = {{15{1'b0}}, or_3_out};  // Bit_Extender bit_extender_5
  Multiplexer #(.select(3), .width(16), .enable("false")) multiplexer_1 (
    .in0(adder_1_out), .in1(adder_1_out), .in2(bit_extender_2_out), .in3(bit_extender_3_out),
    .in4(bit_extender_4_out), .in5(bit_extender_5_out), .out(SECOND_HALF), .sel(ALU_CONT[2:0]));  // open: in6, in7
  Multiplexer #(.select(3), .width(16), .enable("false")) multiplexer_2 (
    .in0(AND_out), .in1(OR_out), .in2(not_3_out), .in3(XOR_2_out), .in4(SL), .in5(SR), .in6(SRA), .in7(R),
    .out(FIRST_HALF), .sel(ALU_CONT[2:0]));
  Multiplexer #(.width(16), .enable("false")) multiplexer_3 (
    .in0(FIRST_HALF), .in1(SECOND_HALF), .out(out_4), .sel(ALU_CONT[3]));

  // Other names for the same wires on the sheet: HALF_SELECTOR = ALU_CONT[3]; SELECTOR[2:0] = ALU_CONT[2:0]
endmodule
