// Logisim project new one.circ as structural Verilog: 8 circuits, main circuit CPU
module data_inst (
  input  [11:0] in_1,
  output [15:0] out_2
);

  wire clock_1_out;

  Clock clock_1 (.out(clock_1_out));
  ROM #(.addrWidth(12), .dataWidth(16)) rom_1 (.addr(in_1), .data(out_2));  // open: sel

  // Notes on the sheet:
  //   Instruction_Memory
endmodule

module data_memory (
  input  [15:0] in_1,
  input  [15:0] in_2,
  input  in_3,
  input  in_4,
  output [15:0] out_5
);

  wire clock_1_out;

  Clock clock_1 (.out(clock_1_out));
  RAM #(.addrWidth(12), .dataWidth(16), .bus("separate")) ram_1 (
    .addr(in_1[11:0]), .din(in_2), .data(out_5), .str(in_3), .clk(clock_1_out), .ld(in_4));  // open: sel, clr

  // Notes on the sheet:
  //   Data_Memory
endmodule

module CPU (
);

  wire ALUSrc, JALR, JumpCtrl, MemoryRead, MemoryReg, MemoryWrite, RegWrite;
  wire [1:0] JAL, RegDst;
  wire [2:0] BrancheSelect, multiplexer_2_out;
  wire [3:0] ALU_CONT, Opcode;
  wire [11:0] DataLUI, main_1_p4, multiplexer_1_out, shifter_1_out;
  wire [15:0] bit_extender_1_out, bit_extender_2_out, bit_extender_3_out, data_memory_1_out_5,
       multiplexer_5_out, RA, RB, reg_file_1_p5, reg_file_1_p8, reg_file_1_p10;

  Multiplexer #(.width(12), .enable("false")) multiplexer_1 (
    .in0(DataLUI), .in1(RA[11:0]), .out(multiplexer_1_out), .sel(JALR));
  Shifter #(.width(12)) shifter_1 (.in(DataLUI), .\dist (4'b0010), .out(shifter_1_out));
  // pc_main main_1: pin names not known; wires that end beside it: multiplexer_1_out, RA, RB, main_1_p4, BrancheSelect, JumpCtrl
  assign bit_extender_1_out = {{4{1'b0}}, main_1_p4};  // Bit_Extender bit_extender_1
  assign bit_extender_2_out = {{4{1'b0}}, shifter_1_out};  // Bit_Extender bit_extender_2
  data_inst data_inst_1 (.in_1(main_1_p4), .out_2({Opcode, DataLUI}));
  Multiplexer #(.select(2), .width(3), .enable("false")) multiplexer_2 (
    .in0(DataLUI[8:6]), .in1(DataLUI[5:3]), .in2(3'b111), .in3(3'b001), .out(multiplexer_2_out), .sel(RegDst));
  // Reg_File reg_file_1: pin names not known; wires that end beside it: DataLUI[11:9], DataLUI[8:6], multiplexer_2_out, RegWrite, reg_file_1_p5, RA, RB, reg_file_1_p8, ALU_CONT, reg_file_1_p10
  assign bit_extender_3_out = {{10{DataLUI[5]}}, DataLUI[5:0]};  // Bit_Extender bit_extender_3
  Multiplexer #(.select(2), .width(16), .enable("false")) multiplexer_3 (
    .in0(multiplexer_5_out), .in1(bit_extender_1_out), .in2(bit_extender_2_out), .out(reg_file_1_p5),
    .sel(JAL));  // open: in3
  Multiplexer #(.width(16), .enable("false")) multiplexer_4 (
    .in0(RB), .in1(bit_extender_3_out), .out(reg_file_1_p8), .sel(ALUSrc));
  // ll ll_1: pin names not known; wires that end beside it: DataLUI[8:6], RA, DataLUI[2:0], Opcode
  // alu_main main_2: pin names not known; wires that end beside it: RA, reg_file_1_p8, ALU_CONT, reg_file_1_p10
  data_memory data_memory_1 (
    .in_1(reg_file_1_p10), .in_2(RB), .in_3(MemoryWrite), .in_4(MemoryRead), .out_5(data_memory_1_out_5));
  Multiplexer #(.width(16), .enable("false")) multiplexer_5 (
    .in0(reg_file_1_p10), .in1(data_memory_1_out_5), .out(multiplexer_5_out), .sel(MemoryReg));

  // Other names for the same wires on the sheet: Funct[2:0] = DataLUI[2:0]
endmodule

module jj (
  input  [5:0] in_1
);
endmodule

module ControlSrc (
  input  z,
  input  x,
  input  c,
  input  v,
  input  g,
  output JALR,
  output JumpCtrl,
  output H,
  output S,
  output RegWrite,
  output M,
  output N,
  output ALUSrc,
  output MemoryWrite,
  output MemoryRead,
  output MemoryReg
);

  wire and_1_out, and_2_out, and_3_out, and_4_out, and_5_out, and_6_out, and_7_out, and_8_out, and_9_out,
       and_10_out, and_11_out, and_12_out, and_13_out, and_14_out, and_15_out, and_16_out, and_17_out,
       and_18_out, and_19_out, and_20_out, and_21_out, and_23_out, and_24_out, and_25_out, and_26_out,
       and_28_out, and_29_out, not_1_out, not_2_out, not_3_out, not_4_out, not_5_out, not_6_out, not_7_out,
       not_8_out, not_9_out, not_10_out, not_11_out, not_12_out, not_13_out, not_14_out, not_15_out,
       not_17_out, not_18_out, not_19_out, not_20_out, or_3_out, or_4_out, or_5_out;

  not not_1 (not_1_out, z);
  not not_2 (not_2_out, c);
  not not_3 (not_3_out, c);
  not not_4 (not_4_out, c);
  not not_5 (not_5_out, g);
  not not_6 (not_6_out, z);
  not not_7 (not_7_out, v);
  not not_8 (not_8_out, c);
  not not_9 (not_9_out, g);
  not not_10 (not_10_out, x);
  not not_11 (not_11_out, c);
  not not_12 (not_12_out, g);
  not not_13 (not_13_out, c);
  not not_14 (not_14_out, x);
  not not_15 (not_15_out, c);
  not not_16 (MemoryRead, g);
  not not_17 (not_17_out, x);
  and and_1 (and_1_out, not_1_out, x);
  and and_2 (and_2_out, c, v);
  and and_3 (and_3_out, z, x);
  and and_4 (and_4_out, not_2_out, g);
  and and_5 (and_5_out, z, x);
  and and_6 (and_6_out, not_3_out, v);
  and and_7 (and_7_out, x, not_4_out);
  and and_8 (and_8_out, v, not_5_out);
  and and_9 (and_9_out, not_6_out, not_7_out);
  and and_10 (and_10_out, not_8_out, not_9_out);
  not not_18 (not_18_out, z);
  and and_11 (and_11_out, not_10_out, c);
  and and_12 (and_12_out, x, not_11_out);
  and and_13 (and_13_out, z, x);
  and and_14 (and_14_out, v, not_12_out);
  and and_15 (and_15_out, x, c);
  and and_16 (and_16_out, z, not_13_out);
  and and_17 (and_17_out, z, not_14_out);
  and and_18 (and_18_out, not_15_out, g);
  and and_19 (and_19_out, z, not_17_out);
  not not_19 (not_19_out, c);
  and and_20 (and_20_out, and_1_out, and_2_out);
  or or_1 (JumpCtrl, and_20_out, and_21_out);
  and and_21 (and_21_out, and_3_out, and_4_out);
  and and_22 (H, and_5_out, and_6_out);
  not not_20 (not_20_out, z);
  or or_2 (S, not_20_out, and_23_out);
  and and_23 (and_23_out, and_7_out, and_8_out);
  or or_3 (or_3_out, and_9_out, and_10_out);
  or or_4 (or_4_out, or_3_out, and_24_out);
  and and_24 (and_24_out, not_18_out, g);
  and and_25 (and_25_out, and_11_out, v);
  or or_5 (or_5_out, and_25_out, and_26_out);
  and and_26 (and_26_out, and_12_out, v);
  and and_27 (M, and_13_out, and_14_out);
  and and_28 (and_28_out, and_15_out, v);
  or or_6 (N, and_28_out, and_29_out);
  and and_29 (and_29_out, and_16_out, g);
  and and_30 (MemoryWrite, and_17_out, and_18_out);
  and and_31 (MemoryReg, and_19_out, not_19_out);
  or or_7 (RegWrite, or_4_out, or_5_out);

  assign ALUSrc = z;
  assign JALR = c;
endmodule

module ALUConrol (
  input  z,
  input  x,
  input  c,
  input  v,
  input  g,
  output A,
  output B,
  output C_2,
  output D
);

  wire and_1_out, and_4_out, and_5_out, and_6_out, and_7_out, and_8_out, and_9_out, and_10_out, and_11_out,
       and_12_out, not_1_out, not_2_out, not_3_out, not_4_out, not_5_out, not_6_out, not_7_out, not_8_out,
       not_9_out, not_10_out, or_1_out;

  not not_1 (not_1_out, x);
  not not_2 (not_2_out, z);
  not not_3 (not_3_out, z);
  not not_4 (not_4_out, x);
  not not_5 (not_5_out, z);
  and and_1 (and_1_out, z, not_1_out);
  not not_6 (not_6_out, c);
  not not_7 (not_7_out, c);
  not not_8 (not_8_out, v);
  not not_9 (not_9_out, g);
  and and_2 (B, not_2_out, c);
  and and_3 (C_2, not_3_out, v);
  not not_10 (not_10_out, z);
  and and_4 (and_4_out, not_4_out, c);
  and and_5 (and_5_out, v, g);
  and and_6 (and_6_out, not_5_out, x);
  or or_1 (or_1_out, and_6_out, and_7_out);
  and and_7 (and_7_out, and_1_out, not_6_out);
  and and_8 (and_8_out, z, not_7_out);
  and and_9 (and_9_out, and_8_out, and_10_out);
  and and_10 (and_10_out, not_8_out, not_9_out);
  and and_11 (and_11_out, not_10_out, g);
  or or_2 (D, and_11_out, and_12_out);
  and and_12 (and_12_out, and_4_out, and_5_out);
  or or_3 (A, or_1_out, and_9_out);
endmodule

module BranchSelect (
  input  z,
  input  x,
  input  c,
  input  v,
  input  g,
  output Q,
  output W,
  output E
);

  wire and_1_out, and_2_out, and_3_out, and_4_out, and_5_out, and_6_out, and_7_out, and_8_out, and_9_out,
       and_10_out, and_11_out, and_12_out, and_14_out, and_15_out, and_16_out, and_17_out, and_18_out,
       not_1_out, not_2_out, not_3_out, not_4_out, not_5_out, not_6_out, not_7_out, or_2_out;

  not not_1 (not_1_out, g);
  not not_2 (not_2_out, v);
  not not_3 (not_3_out, x);
  not not_4 (not_4_out, v);
  not not_5 (not_5_out, g);
  not not_6 (not_6_out, v);
  and and_1 (and_1_out, z, x);
  and and_2 (and_2_out, c, not_1_out);
  and and_3 (and_3_out, z, x);
  and and_4 (and_4_out, c, v);
  and and_5 (and_5_out, z, c);
  and and_6 (and_6_out, not_2_out, g);
  and and_7 (and_7_out, z, not_3_out);
  and and_8 (and_8_out, not_4_out, not_5_out);
  and and_9 (and_9_out, z, x);
  and and_10 (and_10_out, c, not_6_out);
  not not_7 (not_7_out, g);
  and and_11 (and_11_out, and_1_out, and_2_out);
  or or_1 (Q, and_11_out, and_12_out);
  and and_12 (and_12_out, and_3_out, and_4_out);
  and and_13 (W, and_5_out, and_6_out);
  and and_14 (and_14_out, and_7_out, and_8_out);
  or or_2 (or_2_out, and_14_out, and_15_out);
  and and_15 (and_15_out, and_9_out, and_10_out);
  and and_16 (and_16_out, z, x);
  and and_17 (and_17_out, and_16_out, and_18_out);
  and and_18 (and_18_out, c, not_7_out);
  or or_3 (E, or_2_out, and_17_out);
endmodule

module BranchSelect1 (
  input  z,
  input  x,
  input  c,
  input  v,
  input  g,
  output Q,
  output W,
  output E
);

  wire and_1_out, and_2_out, and_3_out, and_4_out, and_5_out, and_6_out, and_7_out, not_1_out, not_2_out,
       not_3_out, not_4_out, not_5_out, not_6_out, not_7_out, not_8_out, not_9_out;

  not not_1 (not_1_out, g);
  not not_2 (not_2_out, x);
  not not_3 (not_3_out, v);
  not not_4 (not_4_out, v);
  not not_5 (not_5_out, x);
  not not_6 (not_6_out, v);
  not not_7 (not_7_out, g);
  not not_8 (not_8_out, v);
  not not_9 (not_9_out, g);
  and and_1 (and_1_out, z, x, c, not_1_out);
  and and_2 (and_2_out, z, x, c, v);
  and and_3 (and_3_out, z, not_2_out, not_3_out, g);
  and and_4 (and_4_out, z, x, c, not_4_out);
  and and_5 (and_5_out, z, not_5_out, not_6_out, not_7_out);
  and and_6 (and_6_out, z, x, c, not_8_out, g);
  and and_7 (and_7_out, z, x, c, v, not_9_out);
  or or_1 (Q, and_1_out, and_2_out);
  or or_2 (W, and_3_out, and_4_out);
  or or_3 (E, and_5_out, and_6_out, and_7_out);
endmodule
