// Logisim project pc.circ as structural Verilog: 1 circuit, main circuit main
module main (
  input  jump,
  input  [11:0] jump_or_branch_value,
  input  in_3,
  input  [15:0] in_4,
  input  in_5,
  input  [15:0] in_6,
  input  [2:0] in_7,
  output [11:0] out_8,
  output [11:0] pc,
  output out_10
);

  wire comparator_1_eq, comparator_1_gt, comparator_1_lt, not_1_out, not_2_out, or_1_out, or_2_out;
  wire [11:0] adder_2_out, bit_extender_1_out, multiplexer_1_out, multiplexer_3_out, shifter_1_out;

  not not_1 (not_1_out, in_3);
  Register #(.width(12)) register_1 (.D(multiplexer_3_out), .en(not_1_out), .Q(pc), .clk(in_5));  // open: clr
  Adder #(.width(12)) adder_1 (.a(12'h2), .b(pc), .out(out_8));  // open: cin, cout
  Comparator #(.width(16)) comparator_1 (
    .a(in_4), .b(in_6), .gt(comparator_1_gt), .eq(comparator_1_eq), .lt(comparator_1_lt));
  not not_2 (not_2_out, comparator_1_eq);
  or or_1 (or_1_out, comparator_1_gt, comparator_1_eq);
  or or_2 (or_2_out, comparator_1_eq, comparator_1_lt);
  Multiplexer #(.width(12), .enable("false")) multiplexer_1 (
    .in0(out_8), .in1(jump_or_branch_value), .out(multiplexer_1_out), .sel(jump));
  assign bit_extender_1_out = {{6{jump_or_branch_value[5]}}, jump_or_branch_value[5:0]};  // Bit_Extender bit_extender_1
  Multiplexer #(.select(3), .enable("false")) multiplexer_2 (
    .in0(1'b0), .in1(comparator_1_eq), .in2(not_2_out), .in3(comparator_1_lt), .in4(comparator_1_gt),
    .in5(or_1_out), .in6(or_2_out), .in7(1'b0), .out(out_10), .sel(in_7));
  Multiplexer #(.width(12), .enable("false")) multiplexer_3 (
    .in0(multiplexer_1_out), .in1(adder_2_out), .out(multiplexer_3_out), .sel(out_10));
  Shifter #(.width(12)) shifter_1 (.in(bit_extender_1_out), .\dist (4'b0001), .out(shifter_1_out));
  Adder #(.width(12)) adder_2 (.a(pc), .b(shifter_1_out), .out(adder_2_out));  // open: cin, cout
endmodule
